// Digital circuit Restador4bits.dig as structural Verilog
module Restador4bits (
  input  A0,
  input  B0,
  input  A1,
  input  B1,
  input  A2,
  input  B2,
  input  A3,
  input  B3,
  output S0,
  output S3,
  output C_0ut,
  output S1,
  output S2
);

  wire mediorestador_1_c_out, restadorcompleto_1_c_out, restadorcompleto_2_c_out;

  MedioRestador mediorestador_1 (.A(A0), .B(B0), .S(S0), .C_out(mediorestador_1_c_out));
  RestadorCompleto restadorcompleto_1 (
    .A(A1), .B(B1), .C_in(mediorestador_1_c_out), .S(S1), .C_out(restadorcompleto_1_c_out));
  RestadorCompleto restadorcompleto_2 (
    .A(A2), .B(B2), .C_in(restadorcompleto_1_c_out), .S(S2), .C_out(restadorcompleto_2_c_out));
  RestadorCompleto restadorcompleto_3 (.A(A3), .B(B3), .C_in(restadorcompleto_2_c_out), .S(S3), .C_out(C_0ut));
endmodule
