// Digital circuit MedioRestador.dig as structural Verilog
module MedioRestador (
  input  A,
  input  B,
  output S,
  output C_out
);

  wire not_1_out;

  not not_1 (not_1_out, A);
  xor xor_1 (S, A, B);
  and and_1 (C_out, B, not_1_out);
endmodule
