// Digital circuit RestadorCompleto.dig as structural Verilog
module RestadorCompleto (
  input  A,
  input  B,
  input  C_in,
  output S,
  output C_out
);

  wire and_1_out, and_2_out, not_1_out, or_1_out;

  xor xor_1 (S, A, B, C_in);
  or or_1 (or_1_out, B, C_in);
  and and_1 (and_1_out, C_in, B);
  not not_1 (not_1_out, A);
  and and_2 (and_2_out, or_1_out, not_1_out);
  or or_2 (C_out, and_2_out, and_1_out);
endmodule
