// Digital circuit restSum.dig as structural Verilog
module restSum (
  input  A1,
  input  A2,
  input  A3,
  input  A4,
  input  B1,
  input  B2,
  input  B3,
  input  B4,
  input  Ci,
  input  Ctrl,
  output S1,
  output S2,
  output S3,
  output C0,
  output S4
);

  wire and_1_out, and_2_out, and_3_out, and_4_out, and_5_out, and_6_out, and_7_out, and_8_out, and_9_out,
       and_10_out, and_11_out, and_12_out, and_13_out, and_14_out, and_15_out, and_16_out, and_17_out,
       not_1_out, not_2_out, not_3_out, not_4_out, not_5_out, not_6_out, not_7_out, not_8_out,
       restador4bits_1_c_0ut, restador4bits_1_s0, restador4bits_1_s1, restador4bits_1_s2, restador4bits_1_s3,
       sumador_4bits_1_co, sumador_4bits_1_s1, sumador_4bits_1_s2, sumador_4bits_1_s3, sumador_4bits_1_s4;

  not not_1 (not_1_out, Ctrl);
  not not_2 (not_2_out, Ctrl);
  not not_3 (not_3_out, Ctrl);
  not not_4 (not_4_out, Ctrl);
  not not_5 (not_5_out, Ctrl);
  not not_6 (not_6_out, Ctrl);
  not not_7 (not_7_out, Ctrl);
  not not_8 (not_8_out, Ctrl);
  and and_1 (and_1_out, A1, Ctrl);
  and and_2 (and_2_out, A2, Ctrl);
  and and_3 (and_3_out, A3, Ctrl);
  and and_4 (and_4_out, A4, Ctrl);
  and and_5 (and_5_out, B1, Ctrl);
  and and_6 (and_6_out, B2, Ctrl);
  and and_7 (and_7_out, B3, Ctrl);
  and and_8 (and_8_out, B4, Ctrl);
  and and_9 (and_9_out, Ci, Ctrl);
  and and_10 (and_10_out, A1, not_1_out);
  and and_11 (and_11_out, A2, not_2_out);
  and and_12 (and_12_out, A3, not_3_out);
  and and_13 (and_13_out, A4, not_4_out);
  and and_14 (and_14_out, B1, not_5_out);
  and and_15 (and_15_out, B2, not_6_out);
  and and_16 (and_16_out, B3, not_7_out);
  and and_17 (and_17_out, B4, not_8_out);
  Sumador_4bits sumador_4bits_1 (
    .A1(and_1_out), .B1(and_5_out), .Ci(and_9_out), .A2(and_2_out), .B2(and_6_out), .A3(and_3_out),
    .B3(and_7_out), .A4(and_4_out), .B4(and_8_out), .S1(sumador_4bits_1_s1), .S2(sumador_4bits_1_s2),
    .S3(sumador_4bits_1_s3), .S4(sumador_4bits_1_s4), .Co(sumador_4bits_1_co));
  Restador4bits restador4bits_1 (
    .A0(and_10_out), .B0(and_14_out), .A1(and_11_out), .B1(and_15_out), .A2(and_12_out), .B2(and_16_out),
    .A3(and_13_out), .B3(and_17_out), .S0(restador4bits_1_s0), .S3(restador4bits_1_s3),
    .C_0ut(restador4bits_1_c_0ut), .S1(restador4bits_1_s1), .S2(restador4bits_1_s2));
  or or_1 (S1, sumador_4bits_1_s1, restador4bits_1_s0);
  or or_2 (S2, sumador_4bits_1_s2, restador4bits_1_s1);
  or or_3 (S3, sumador_4bits_1_s3, restador4bits_1_s2);
  or or_4 (S4, sumador_4bits_1_s4, restador4bits_1_s3);
  or or_5 (C0, sumador_4bits_1_co, restador4bits_1_c_0ut);
endmodule
