// Digital circuit Fulladder.dig as structural Verilog
module Fulladder (
  input  A,
  input  B,
  input  Ci,
  output Co,
  output S
);

  wire and_1_out, and_2_out, or_1_out, xor_1_out;

  or or_1 (or_1_out, A, B);
  xor xor_1 (xor_1_out, A, B);
  and and_1 (and_1_out, A, B);
  and and_2 (and_2_out, or_1_out, Ci);
  xor xor_2 (S, xor_1_out, Ci);
  or or_2 (Co, and_1_out, and_2_out);
endmodule
