// Digital circuit Sumador_4bits.dig as structural Verilog
module Sumador_4bits (
  input  A1,
  input  B1,
  input  Ci,
  input  A2,
  input  B2,
  input  A3,
  input  B3,
  input  A4,
  input  B4,
  output S1,
  output S2,
  output S3,
  output S4,
  output Co
);

  wire fulladder_1_co, fulladder_2_co, fulladder_3_co;

  Fulladder fulladder_1 (.A(A1), .B(B1), .Ci(Ci), .Co(fulladder_1_co), .S(S1));
  Fulladder fulladder_2 (.A(A2), .B(B2), .Ci(fulladder_1_co), .Co(fulladder_2_co), .S(S2));
  Fulladder fulladder_3 (.A(A3), .B(B3), .Ci(fulladder_2_co), .Co(fulladder_3_co), .S(S3));
  Fulladder fulladder_4 (.A(A4), .B(B4), .Ci(fulladder_3_co), .Co(Co), .S(S4));
endmodule
